// Digital circuit BeanBoardSPI.dig as structural Verilog
module BeanBoardSPI (
  input  DATA_WRITE,
  input  CLK,
  input  enable,
  input  CTRL_WRITE,
  input  D0,
  input  D1,
  input  D2,
  input  D3,
  input  D4,
  input  D5,
  input  D6,
  input  D7,
  input  RD,
  input  WR,
  input  IORQ,
  input  A1,
  input  A2,
  input  A3,
  input  DATA_READ,
  input  SER_IN,
  output CS0,
  output CS1,
  output CS2,
  output CS3,
  output CS4,
  output CS5,
  output CS6,
  output SRESET,
  output D0_2,
  output D1_2,
  output D2_2,
  output D3_2,
  output D4_2,
  output D5_2,
  output D6_2,
  output D7_2,
  output SER_OUT,
  output SCK
);

  wire _74165_1_pin9, _74165_1_pin10, _74165_3_pin10, clk_t, clk_t_t, ctrl_write_t, data_write_t, di0, di1,
       di2, di3, di4, di5, di6, di7;

  and and_1 (clk_t_t, CLK, enable);
  not not_1 (clk_t, clk_t_t);
  // ScopeTrigger scopetrigger_1: pin names not known; wires that end beside it: clk_t_t
  assign D0_2 = ~WR ? D0 : 1'bz;  // DriverInvSel driverinvsel_1
  assign D1_2 = ~WR ? D1 : 1'bz;  // DriverInvSel driverinvsel_2
  assign D2_2 = ~WR ? D2 : 1'bz;  // DriverInvSel driverinvsel_3
  assign D3_2 = ~WR ? D3 : 1'bz;  // DriverInvSel driverinvsel_4
  assign D4_2 = ~WR ? D4 : 1'bz;  // DriverInvSel driverinvsel_5
  assign D5_2 = ~WR ? D5 : 1'bz;  // DriverInvSel driverinvsel_6
  assign D6_2 = ~WR ? D6 : 1'bz;  // DriverInvSel driverinvsel_7
  assign D7_2 = ~WR ? D7 : 1'bz;  // DriverInvSel driverinvsel_8
  not not_2 (data_write_t, DATA_WRITE);
  not not_3 (ctrl_write_t, CTRL_WRITE);
  _74165 _74165_1 (
    .pin1(DATA_WRITE), .pin2(clk_t_t), .pin3(1'b1), .pin4(1'b1), .pin5(1'b1), .pin6(1'b0), .pin8(1'b0),
    .pin9(_74165_1_pin9), .pin10(_74165_1_pin10), .pin11(1'b1), .pin12(1'b1), .pin13(1'b1), .pin14(1'b1),
    .pin15(data_write_t), .pin16(1'b1));  // open: pin7
  _74165 _74165_2 (
    .pin1(DATA_WRITE), .pin2(clk_t_t), .pin3(1'b0), .pin4(1'b0), .pin5(1'b0), .pin6(1'b1), .pin8(1'b0),
    .pin9(_74165_1_pin10), .pin10(1'b0), .pin11(1'b0), .pin12(1'b0), .pin13(1'b0), .pin14(1'b0),
    .pin15(data_write_t), .pin16(1'b1));  // open: pin7
  _74165 _74165_3 (
    .pin1(DATA_WRITE), .pin2(clk_t_t), .pin3(D5_2), .pin4(D6_2), .pin5(D7_2), .pin6(1'b0), .pin8(1'b0),
    .pin9(SER_OUT), .pin10(_74165_3_pin10), .pin11(D1_2), .pin12(D2_2), .pin13(D3_2), .pin14(D4_2),
    .pin15(data_write_t), .pin16(1'b1));  // open: pin7
  _74165 _74165_4 (
    .pin1(DATA_WRITE), .pin2(clk_t_t), .pin3(1'b0), .pin4(1'b0), .pin5(1'b0), .pin6(D0_2), .pin8(1'b0),
    .pin9(_74165_3_pin10), .pin10(1'b0), .pin11(1'b0), .pin12(1'b0), .pin13(1'b0), .pin14(1'b0),
    .pin15(data_write_t), .pin16(1'b1));  // open: pin7
  _74164 _74164_1 (
    .pin1(SER_IN), .pin2(_74165_1_pin9), .pin3(di0), .pin4(di1), .pin5(di2), .pin6(di3), .pin7(1'b0),
    .pin8(SCK), .pin9(DATA_WRITE), .pin10(di4), .pin11(di5), .pin12(di6), .pin13(di7), .pin14(1'b1));
  and and_2 (SCK, _74165_1_pin9, clk_t);
  Switch #(.Closed("true")) switch_1 (.A(SER_OUT), .B(SER_IN));
  _74373 _74373_1 (
    .pin1(1'b0), .pin2(SRESET), .pin3(D0_2), .pin4(D1_2), .pin5(CS0), .pin6(CS1), .pin7(D2_2), .pin8(D3_2),
    .pin9(CS2), .pin10(1'b0), .pin11(ctrl_write_t), .pin12(CS3), .pin13(D4_2), .pin14(D5_2), .pin15(CS4),
    .pin16(CS5), .pin17(D6_2), .pin18(D7_2), .pin19(CS6), .pin20(1'b1));
  _74244 _74244_1 (
    .pin1(DATA_READ), .pin2(di0), .pin3(D7_2), .pin4(di1), .pin5(D6_2), .pin6(di2), .pin7(D5_2), .pin8(di3),
    .pin9(D4_2), .pin10(1'b0), .pin11(di4), .pin12(D3_2), .pin13(di5), .pin14(D2_2), .pin15(di6),
    .pin16(D1_2), .pin17(di7), .pin18(D0_2), .pin19(DATA_READ), .pin20(1'b1));

  // Other names for the same wires on the sheet: cs_0 = CS0; cs_1 = CS1; cs_2 = CS2; cs_3 = CS3; cs_4 = CS4;
  //   cs_5 = CS5; cs_6 = CS6; d0_t = D0_2; d1_t = D1_2; d2_t = D2_2; d3_t = D3_2; d4_t = D4_2; d5_t = D5_2;
  //   d6_t = D6_2; d7_t = D7_2; ser_clk = SCK

  // Notes on the sheet:
  //   DATA_WRITE: default 1
  //   enable: default 1
  //   CTRL_WRITE: default 1
  //   D0: default 1
  //   D1: default 1
  //   D2: default 1
  //   D3: default 1
  //   D4: default 1
  //   D5: default 1
  //   D6: default 1
  //   D7: default 1
  //   RD: default 1
  //   WR: default 1
  //   IORQ: default 1
  //   A3: default 1
  //   DATA_READ: default 1
  //   Z80
  //   SPI
  //   Ctrl
  //   Bits
  //   reset
  //   cs0
  //   cs1
  //   cs2
  //   cs3
  //   cs4
  //   cs5
  //   cs6
  //   Counter
  //   Serial Out
  //   Serial In
  //   SPI Control Register
  //   Data read buffer
endmodule
